# Fritzing sketch Circuit Sketch (saved by Fritzing 0.9.10b)
breadboards: 1

parts:
  U1 = ESP32-38PinWide [part_number=ESP32-38PinWide]
  LED1 = RGB LED - (4 legs) [package="5 mm [THT]"]
  元件1 = InvenSense MPU6050

nets:
  N1: U1.3.3, 元件1.VCC
  GND: U1.GND, LED1.blue_cathode, 元件1.GND
  N2: U1.GPIO16, LED1.red_cathode
  N3: U1.GPIO17, LED1.common_anode
  N4: U1.GPIO18, LED1.green_cathode
  N5: U1.GPIO21, 元件1.SDA
  N6: U1.GPIO22, 元件1.SCL

custom parts:
  ESP32-38PinWide: Generic 38-Pin ESP32 with wide format (only access to one side of pins on a breadboard) based on Stephen Lilley's HiLetgo ESP-WROOM-32 ESP32 ESP-32S Development Board.
